// Logisim project computer.circ as structural Verilog: 4 circuits, main circuit main
module main (
  input  [7:0] input_pins,
  output [7:0] output_pins
);

  wire AI, alu_c_ezero, alu_c_gzero, ALUO, AO, CI, clock_1_out, CO, DI, DO, IO, IRI, MARI, OI, pc_low_carry,
       PCC, PCHI, RAMI, RAMO, RESET, ROMO, ROMOT2;
  wire [2:0] cu_c_outflag;
  wire [2:2] or_3_out;
  wire [3:0] cu_c_inflag;
  wire [7:0] alu_c_aluout, and_1_out, and_2_out, areg_q, bit_extender_1_out, bit_extender_2_out, CINS,
       CINSTEMP, creg_q, dreg_q, ireg_q, mar_q, multiplexer_1_out, or_2_out, pc_rom_data, ram_c_dout;
  wire [15:0] PCIN, PCOUT;

  Clock clock_1 (.out(clock_1_out));
  Counter pc_low (
    .clr(RESET), .load(PCHI), .up(1'b1), .count(PCC), .clk(clock_1_out), .D(PCIN[7:0]), .carry(pc_low_carry),
    .Q(PCOUT[7:0]));
  ROM #(.addrWidth(16)) pc_rom (.addr(PCOUT), .data(pc_rom_data));
  Register mar (.D(or_2_out), .en(MARI), .clk(clock_1_out), .Q(mar_q), .clr(RESET));
  cu cu_c (
    .IRIN(or_2_out), .IRI_IN(IRI), .CLK(clock_1_out), .RESET(RESET), .CUOUT(CINSTEMP), .INFLAG(cu_c_inflag),
    .OUTFLAG(cu_c_outflag), .PCC(PCC), .IRI_OUT(IRI));
  Decoder #(.select(3), .enable("false")) decoder_1 (
    .out1(IO), .out2(AO), .out3(CO), .out4(DO), .out5(ROMOT2), .out6(RAMO), .sel(cu_c_outflag));  // open: out0, out7
  RAM #(.databus("bibus")) ram_c (
    .addr(mar_q), .we(RAMI), .oe(RAMO), .clk(clock_1_out), .din(or_2_out), .dout(ram_c_dout));
  or or_1 (ROMO, IRI, ROMOT2);
  Counter pc_high (
    .clr(RESET), .load(PCHI), .up(1'b1), .clk(pc_low_carry), .D(PCIN[15:8]), .Q(PCOUT[15:8]));  // open: count, carry
  Button reset_button (.out(RESET));
  assign and_1_out = pc_rom_data & bit_extender_1_out;  // AND_Gate and_1, 8 bits wide
  assign bit_extender_1_out = {{7{ROMO}}, ROMO};  // Bit_Extender bit_extender_1
  Decoder #(.select(4), .enable("false")) decoder_2 (
    .out1(OI), .out2(RAMI), .out3(MARI), .out4(AI), .out5(CI), .out6(DI), .sel(cu_c_inflag));  // open: out0, out7, out8, out9, out10, out11, out12, out13, out14, out15
  assign or_2_out = ram_c_dout | and_1_out | alu_c_aluout | and_2_out;  // OR_Gate or_2, 8 bits wide
  Register areg (.D(or_2_out), .en(AI), .clk(clock_1_out), .Q(areg_q), .clr(RESET));
  Register creg (.D(or_2_out), .en(CI), .clk(clock_1_out), .Q(creg_q), .clr(RESET));
  Register dreg (.D(or_2_out), .en(DI), .clk(clock_1_out), .Q(dreg_q), .clr(RESET));
  Register oreg (.D(or_2_out), .en(OI), .clk(clock_1_out), .Q(output_pins), .clr(RESET));
  Register ireg (.D(input_pins), .en(1'b1), .clk(clock_1_out), .Q(ireg_q), .clr(RESET));
  or or_3 (or_3_out[2], CO, DO);
  assign and_2_out = ireg_q & bit_extender_2_out;  // AND_Gate and_2, 8 bits wide
  assign CINS = CINSTEMP | {{5{1'b0}}, or_3_out[2], {2{AO}}};  // OR_Gate or_4, 8 bits wide
  or or_5 (ALUO, AO, CO, DO);
  alu alu_c (
    .A(areg_q), .B(multiplexer_1_out), .CLK(clock_1_out), .RESET(RESET), .CINS(CINS), .OE(ALUO),
    .GZERO(alu_c_gzero), .EZERO(alu_c_ezero), .ALUOUT(alu_c_aluout));
  Multiplexer #(.width(8), .enable("false")) multiplexer_1 (
    .in0(creg_q), .in1(dreg_q), .out(multiplexer_1_out), .sel(DO));
  assign bit_extender_2_out = {{7{1'b0}}, IO};  // Bit_Extender bit_extender_2
  jmp jmp_c (
    .JMPINS(CINS), .GZERO(alu_c_gzero), .EZERO(alu_c_ezero), .PCIN(PCIN), .DATABUS(or_2_out), .PCO(PCHI),
    .PCOUT(PCIN));

  // Other names for the same wires on the sheet: DOO = DO; PCLI = PCHI

  // Notes on the sheet:
  //   contents of pc_rom (hex, n*v repeats v):
  //   11
  //   Output termination
  //   Data bus
  //   AO,CO,DO Uses a combination of CINS,ALUO and DOO
endmodule

module alu (
  input  [7:0] A,
  input  [7:0] B,
  input  CLK,
  input  RESET,
  input  [7:0] CINS,
  input  OE,
  output GZERO,
  output EZERO,
  output [7:0] ALUOUT
);

  wire adder_1_cout, and_5_out, CARRY, d_ff_1_q, IA, IB, IO, ZA, ZB;
  wire [1:0] CSELECT;
  wire [7:0] adder_1_out, and_1_out, and_2_out, and_3_out, and_4_out, multiplexer_1_out, shifter_1_out,
       shifter_2_out, xor_1_out, xor_2_out;

  assign and_1_out = ~{8{ZA}} & A;  // AND_Gate and_1, 8 bits wide
  assign and_2_out = B & ~{8{ZB}};  // AND_Gate and_2, 8 bits wide
  assign xor_1_out = {8{IA}} ^ and_1_out;  // XOR_Gate xor_1, 8 bits wide
  Adder adder_1 (.a(xor_2_out), .b(xor_1_out), .out(adder_1_out), .cin(and_5_out), .cout(adder_1_cout));
  assign and_3_out = xor_2_out & xor_1_out;  // AND_Gate and_3, 8 bits wide
  Shifter #(.shift("lr")) shifter_1 (.in(xor_2_out), .\dist (xor_1_out[2:0]), .out(shifter_1_out));
  Shifter shifter_2 (.in(xor_2_out), .\dist (xor_1_out[2:0]), .out(shifter_2_out));
  D_Flip_Flop #(.trigger("falling")) d_ff_1 (
    .D(adder_1_cout), .clk(CLK), .Q(d_ff_1_q), .reset(RESET));  // open: Qn, preset
  ROM alu_rom (.addr(and_4_out), .data({CSELECT, CARRY, IO, IB, ZB, IA, ZA}));
  assign and_4_out = CINS & {8{OE}};  // AND_Gate and_4, 8 bits wide
  assign xor_2_out = and_2_out ^ {8{IB}};  // XOR_Gate xor_2, 8 bits wide
  Multiplexer #(.select(2), .width(8), .enable("false")) multiplexer_1 (
    .in0(adder_1_out), .in1(and_3_out), .in2(shifter_1_out), .in3(shifter_2_out), .out(multiplexer_1_out),
    .sel(CSELECT));
  and and_5 (and_5_out, d_ff_1_q, CARRY);
  assign ALUOUT = {8{IO}} ^ multiplexer_1_out;  // XOR_Gate xor_3, 8 bits wide
  or or_1 (GZERO, ALUOUT[7], ALUOUT[6], ALUOUT[5], ALUOUT[4], ALUOUT[3], ALUOUT[2], ALUOUT[1], ALUOUT[0]);
  nor nor_1 (EZERO, ALUOUT[7], ALUOUT[6], ALUOUT[5], ALUOUT[4], ALUOUT[3], ALUOUT[2], ALUOUT[1], ALUOUT[0]);

  // Notes on the sheet:
  //   contents of alu_rom (hex, n*v repeats v):
  //   20*0 c0 43*0 5 1f 7 4 1 14 11 1c 13 1e 1b c 3 0 12 18 80 96 20 40
endmodule

module cu (
  input  [7:0] IRIN,
  input  IRI_IN,
  input  CLK,
  input  RESET,
  output [7:0] CUOUT,
  output [3:0] INFLAG,
  output [2:0] OUTFLAG,
  output PCC,
  output IRI_OUT
);

  wire and_1_out, undriven, undriven_2, xor_1_out;
  wire [1:0] counter_1_q;
  wire [3:0] INSTYPE;
  wire [6:0] bit_extender_1_out, cu_rom_data;
  wire [7:0] bit_extender_2_out;
  wire [7:4] register_1_q;

  Counter #(.width(2), .max('h3)) counter_1 (
    .clr(RESET), .clk(CLK), .Q(counter_1_q));  // open: load, up, count, D, carry
  Register register_1 (.D(IRIN), .en(IRI_IN), .clk(CLK), .Q({register_1_q, INSTYPE}), .clr(RESET));
  ROM #(.dataWidth(7)) cu_rom (.addr({register_1_q, INSTYPE}), .data(cu_rom_data));
  ROM #(.addrWidth(4), .dataWidth(1)) ins_rom (.addr(INSTYPE));  // open: data
  ROM #(.addrWidth(4), .dataWidth(1)) rom_1 (.addr(INSTYPE));  // open: data
  or or_1 (PCC, undriven, and_1_out);
  xor xor_1 (xor_1_out, counter_1_q[1], counter_1_q[0]);
  and and_1 (and_1_out, counter_1_q[1], counter_1_q[0]);
  and and_2 (IRI_OUT, ~counter_1_q[1], ~counter_1_q[0]);  // AND_Gate
  assign {OUTFLAG, INFLAG} = cu_rom_data & bit_extender_1_out;  // AND_Gate and_3, 7 bits wide
  assign bit_extender_1_out = {{6{1'b0}}, xor_1_out};  // Bit_Extender bit_extender_1
  assign bit_extender_2_out = {{7{1'b0}}, undriven_2};  // Bit_Extender bit_extender_2
  assign CUOUT = bit_extender_2_out & {register_1_q, INSTYPE};  // AND_Gate and_4, 8 bits wide

  // Notes on the sheet:
  //   contents of cu_rom (hex, n*v repeats v):
  //   16*0 25 26 34 26 44 45 10*0 5*20 5*30 5*40 0 5*20 5*30 5*40 0 32*34
  //   contents of ins_rom (hex, n*v repeats v):
  //   0 0 1 0 0 0 1
  //   If load or jmp instruction, we should activate PC
  //   on first clock cycle
  //   contents of rom_1 (hex, n*v repeats v):
  //   0 0 5*1
  //   If an OPP, OPP2 or JMP operation then
  //   pipe the input directly to the CUOUT
endmodule

module jmp (
  input  [7:0] JMPINS,
  input  GZERO,
  input  EZERO,
  input  [15:0] PCIN,
  input  [7:0] DATABUS,
  output PCO,
  output [15:0] PCOUT
);

  wire and_1_out, and_2_out, and_3_out, and_4_out, or_1_out, or_2_out;
  wire [6:0] rom_1_data;
  wire [15:0] adder_1_out, bit_extender_1_out;

  ROM #(.dataWidth(7)) rom_1 (.addr(JMPINS), .data(rom_1_data));
  assign bit_extender_1_out = {{8{1'b0}}, DATABUS};  // Bit_Extender bit_extender_1
  and and_1 (and_1_out, ~GZERO, rom_1_data[0]);  // AND_Gate
  or or_1 (or_1_out, and_1_out, rom_1_data[2], and_2_out);
  and and_2 (and_2_out, GZERO, rom_1_data[1]);
  and and_3 (and_3_out, ~EZERO, rom_1_data[3]);  // AND_Gate
  or or_2 (or_2_out, and_3_out, rom_1_data[5], and_4_out);
  and and_4 (and_4_out, EZERO, rom_1_data[4]);
  Adder #(.width(16)) adder_1 (.a(PCIN), .b(bit_extender_1_out), .out(adder_1_out));  // open: cin, cout
  and and_5 (PCO, or_1_out, or_2_out);
  Multiplexer #(.width(16)) multiplexer_1 (
    .in0(bit_extender_1_out), .in1(adder_1_out), .out(PCOUT), .sel(rom_1_data[6]), .en(PCO));

  // Notes on the sheet:
  //   contents of rom_1 (hex, n*v repeats v):
  //   32*0 21 9 14 a 22 21 9 14 a 22 21 9 14 a 22 0 61 49 54 4a 62 61 49 54 4a 62 61 49 54 4a 62
endmodule
