// Logisim project fibonacci_advanced.circ as structural Verilog: 6 circuits, main circuit fibonacci
module fibonacci (
);

  wire button_1_out, button_2_out, clock_1_out, nor_1_out;
  wire [7:0] main_1_output_pins;

  Clock clock_1 (.out(clock_1_out));
  Button button_1 (.out(button_1_out));
  Button button_2 (.out(button_2_out));
  main main_1 (
    .clk(clock_1_out), .reset(button_1_out), .\continue (button_2_out), .output_pins(main_1_output_pins));  // open: input_pins, out_6
  nor nor_1 (nor_1_out, main_1_output_pins[7], main_1_output_pins[6], main_1_output_pins[5], main_1_output_pins[4], main_1_output_pins[3], main_1_output_pins[2], main_1_output_pins[1], main_1_output_pins[0]);
  TTY tty_1 (.data(main_1_output_pins[6:0]), .clk(main_1_output_pins[7]), .clr(nor_1_out));  // open: we
endmodule

module main (
  input  clk,
  input  reset,
  input  \continue ,
  input  [7:0] input_pins,
  output [7:0] output_pins,
  output [7:0] out_6
);

  wire AI, alu_c_carryout, alu_c_cmpo, alu_c_overout, ALUO, and_1_out, AO, c_button_out, CI, clock_1_out,
       cmp_c_cflago, cmp_c_oflago, cmp_c_sflago, cmp_c_zflago, CO, DI, DO, HALT, IO, IRI, JMPO, MARI, OI,
       or_1_out, or_2_out, pc_low_carry, PCC, PCHI, RAMI, RAMO, reset_button_out, RESET_t, ROMO, ROMOT;
  wire [2:0] cu_c_outflag;
  wire [3:0] cu_c_inflag;
  wire [7:0] alu_c_aluout, and_2_out, and_3_out, and_4_out, areg_q, bit_extender_1_out, bit_extender_2_out,
       bit_extender_3_out, CINS, creg_q, dreg_q, ireg_q, mar_q, multiplexer_1_out, or_5_out, pc_rom_data,
       ram_c_dout;
  wire [15:0] PCIN, PCOUT;

  or or_1 (or_1_out, \continue , c_button_out);
  Button c_button (.out(c_button_out));
  and and_1 (and_1_out, ~or_1_out, HALT);  // AND_Gate
  Clock clock_1 (.out(clock_1_out));
  or or_2 (or_2_out, clk, and_1_out, clock_1_out);
  Counter pc_low (
    .clr(RESET_t), .load(PCHI), .up(1'b1), .count(PCC), .clk(or_2_out), .D(PCIN[7:0]), .carry(pc_low_carry),
    .Q(PCOUT[7:0]));
  ROM #(.addrWidth(16)) pc_rom (.addr(PCOUT), .data(pc_rom_data));
  Register mar (.D(or_5_out), .en(MARI), .clk(or_2_out), .Q(mar_q), .clr(RESET_t));
  or or_3 (RESET_t, reset, reset_button_out);
  Button reset_button (.out(reset_button_out));
  cu cu_c (
    .IRIN(or_5_out), .IRI_IN(IRI), .CLK(or_2_out), .RESET(RESET_t), .CUOUT(CINS), .INFLAG(cu_c_inflag),
    .OUTFLAG(cu_c_outflag), .PCC(PCC), .IRI_OUT(IRI));
  RAM #(.databus("bibus")) ram_c (
    .addr(mar_q), .we(RAMI), .clk(or_2_out), .din(or_5_out), .dout(ram_c_dout));  // open: oe
  Decoder #(.select(3), .enable("false")) decoder_1 (
    .out1(IO), .out2(AO), .out3(CO), .out4(DO), .out5(ROMOT), .out6(RAMO), .out7(JMPO), .sel(cu_c_outflag));  // open: out0
  Counter pc_high (
    .clr(RESET_t), .load(PCHI), .up(1'b1), .clk(pc_low_carry), .D(PCIN[15:8]), .Q(PCOUT[15:8]));  // open: count, carry
  or or_4 (ROMO, PCC, ROMOT);
  assign bit_extender_1_out = {{7{ROMO}}, ROMO};  // Bit_Extender bit_extender_1
  assign bit_extender_2_out = {{7{RAMO}}, RAMO};  // Bit_Extender bit_extender_2
  assign and_2_out = pc_rom_data & bit_extender_1_out;  // AND_Gate and_2, 8 bits wide
  assign and_3_out = bit_extender_2_out & ram_c_dout;  // AND_Gate and_3, 8 bits wide
  assign or_5_out = and_3_out | and_2_out | alu_c_aluout | and_4_out;  // OR_Gate or_5, 8 bits wide
  Decoder #(.select(4), .enable("false")) decoder_2 (
    .out1(OI), .out2(RAMI), .out3(MARI), .out4(AI), .out5(CI), .out6(DI), .out15(HALT), .sel(cu_c_inflag));  // open: out0, out7, out8, out9, out10, out11, out12, out13, out14
  Register areg (.D(or_5_out), .en(AI), .clk(or_2_out), .Q(areg_q), .clr(RESET_t));
  Register creg (.D(or_5_out), .en(CI), .clk(or_2_out), .Q(creg_q), .clr(RESET_t));
  Register dreg (.D(or_5_out), .en(DI), .clk(or_2_out), .Q(dreg_q), .clr(RESET_t));
  Register oreg (.D(or_5_out), .en(OI), .clk(or_2_out), .Q(out_6), .clr(RESET_t));
  Register ireg (.D(input_pins), .en(1'b1), .clk(or_2_out), .Q(ireg_q), .clr(RESET_t));
  or or_6 (ALUO, AO, CO, DO);
  Multiplexer #(.width(8), .enable("false")) multiplexer_1 (
    .in0(creg_q), .in1(dreg_q), .out(multiplexer_1_out), .sel(DO));
  assign and_4_out = ireg_q & bit_extender_3_out;  // AND_Gate and_4, 8 bits wide
  assign bit_extender_3_out = {{7{IO}}, IO};  // Bit_Extender bit_extender_3
  alu alu_c (
    .A(areg_q), .B(multiplexer_1_out), .CARRYIN(cmp_c_cflago), .OE(ALUO), .CINS(CINS), .ALUOUT(alu_c_aluout),
    .OVEROUT(alu_c_overout), .CARRYOUT(alu_c_carryout), .CMPO(alu_c_cmpo));
  cmp cmp_c (
    .CMPIN(alu_c_aluout), .OVERFLOW(alu_c_overout), .CARRY(alu_c_carryout), .OE(alu_c_cmpo), .CLK(or_2_out),
    .RESET(RESET_t), .ZFLAGO(cmp_c_zflago), .OFLAGO(cmp_c_oflago), .CFLAGO(cmp_c_cflago),
    .SFLAGO(cmp_c_sflago));
  jmp jmp_c (
    .JMPINS(CINS), .OE(JMPO), .ZIN(cmp_c_zflago), .OIN(cmp_c_oflago), .CIN(cmp_c_cflago), .SIN(cmp_c_sflago),
    .PCIN(PCIN), .DATABUS(or_5_out), .CLK(or_2_out), .RESET(RESET_t), .PCOE(PCHI), .PCOUT(PCIN));

  assign output_pins = out_6;

  // Other names for the same wires on the sheet: DOO = DO; PCLI = PCHI

  // Notes on the sheet:
  //   contents of pc_rom (hex, n*v repeats v):
  //   70 4 71 0 94 90 0 0 0 70 1 71 1 94 90 0 0 0 70 0 71 6 94 90 0 0 0 50 71 5 94 90 0 0 0 71 5 94 81 70
  //   6 5d 93 80 11 71 5 94 81 70 1 5d 93 80 10 70 b 93 80 53 31 0 41 52 5b 14 62 71 a 94 90 0 0 0 70 0 36
  //   0 51 70 1 71 b 94 90 0 0 0 71 5 94 81 70 6 5d 93 80 11 71 5 94 81 70 1 5d 93 92 0 0 0 72 a 95 82 71
  //   5 94 81 70 6 5d 93 92 0 0 0 70 a 93 80 71 64 72 0 71 c 94 90 71 64 5e 38 0 98 10 14 59 11 12 30 0 86
  //   14 26 31 0 a5 71 30 5d b0 71 80 61 b0 71 c 94 80 71 a 72 0 71 c 94 90 71 a 5e 38 0 bf 10 14 59 11 12
  //   30 0 ad 14 26 31 0 cc 71 30 5d b0 71 80 61 b0 71 c 94 80 71 30 5d b0 71 80 61 b0 0 0 0 70 5 93 80 71
  //   0 94 81 59 21 72 5 95 90 33 0 23 30 0 1b
  //   Output termination
  //   Data bus
endmodule

module alu (
  input  [7:0] A,
  input  [7:0] B,
  input  CARRYIN,
  input  OE,
  input  [7:0] CINS,
  output [7:0] ALUOUT,
  output OVEROUT,
  output CARRYOUT,
  output CMPO
);

  wire and_2_out, and_5_out, and_6_out, CARRY, IA, IB, IO, ZA, ZB;
  wire [1:0] CSELECT;
  wire [7:0] adder_1_out, and_1_out, and_3_out, and_4_out, bit_extender_1_out, multiplexer_1_out,
       shifter_1_out, shifter_2_out, xor_1_out, xor_2_out, xor_3_out;
  wire [8:8] alu_rom_data;

  assign and_1_out = ~{8{ZA}} & A;  // AND_Gate and_1, 8 bits wide
  assign xor_1_out = {8{IA}} ^ and_1_out;  // XOR_Gate xor_1, 8 bits wide
  and and_2 (and_2_out, CARRYIN, CARRY);
  ROM #(.dataWidth(9)) alu_rom (.addr(CINS), .data({alu_rom_data[8], CSELECT, CARRY, IO, IB, ZB, IA, ZA}));
  assign and_3_out = B & ~{8{ZB}};  // AND_Gate and_3, 8 bits wide
  assign xor_2_out = and_3_out ^ {8{IB}};  // XOR_Gate xor_2, 8 bits wide
  Adder adder_1 (.a(xor_2_out), .b(xor_1_out), .out(adder_1_out), .cin(and_2_out), .cout(CARRYOUT));
  assign and_4_out = xor_2_out & xor_1_out;  // AND_Gate and_4, 8 bits wide
  Shifter #(.shift("lr")) shifter_1 (.in(xor_2_out), .\dist (xor_1_out[2:0]), .out(shifter_1_out));
  Shifter shifter_2 (.in(xor_2_out), .\dist (xor_1_out[2:0]), .out(shifter_2_out));
  Multiplexer #(.select(2), .width(8), .enable("false")) multiplexer_1 (
    .in0(adder_1_out), .in1(and_4_out), .in2(shifter_1_out), .in3(shifter_2_out), .out(multiplexer_1_out),
    .sel(CSELECT));
  and and_5 (and_5_out, xor_2_out[7], ~xor_3_out[7], xor_1_out[7]);  // AND_Gate
  or or_1 (OVEROUT, and_5_out, and_6_out);
  and and_6 (and_6_out, ~xor_2_out[7], xor_3_out[7], ~xor_1_out[7]);  // AND_Gate
  assign xor_3_out = {8{IO}} ^ multiplexer_1_out;  // XOR_Gate xor_3, 8 bits wide
  and and_7 (CMPO, alu_rom_data[8], OE);
  assign bit_extender_1_out = {{7{OE}}, OE};  // Bit_Extender bit_extender_1
  assign ALUOUT = xor_3_out & bit_extender_1_out;  // AND_Gate and_8, 8 bits wide

  // Other names for the same wires on the sheet: OET = OE

  // Notes on the sheet:
  //   contents of alu_rom (hex, n*v repeats v):
  //   16*0 4 4 4*1 10*5 104 112 112 101 118 100 101 118 100 39*0 105 11f 107 104 101 114 111 11c 113 11e
  //   11b 10c 103 100 112 118 180 15a 120 140 12*105 32*0 4 1 1 4 1 1 10*0 6*5 10*0 4 1 1 13*0 4 1 1
endmodule

module cu (
  input  [7:0] IRIN,
  input  IRI_IN,
  input  CLK,
  input  RESET,
  output [7:0] CUOUT,
  output [3:0] INFLAG,
  output [2:0] OUTFLAG,
  output PCC,
  output IRI_OUT
);

  wire and_2_out, and_3_out, decoder_1_out1, decoder_1_out2, decoder_1_out3, undriven, undriven_2;
  wire [1:0] CUCTR_q;
  wire [6:0] bit_extender_1_out, cu_rom_data;

  Counter #(.width(2), .max('h2), .trigger("falling")) CUCTR (
    .clr(RESET), .clk(CLK), .Q(CUCTR_q));  // open: load, up, count, D, carry
  Register register_1 (.D(IRIN), .en(IRI_IN), .clk(CLK), .Q(CUOUT), .clr(RESET));
  ROM #(.dataWidth(7)) cu_rom (.addr(CUOUT), .data(cu_rom_data));
  ROM #(.addrWidth(4), .dataWidth(1)) ins_rom (.addr(CUOUT[7:4]));  // open: data
  ROM #(.addrWidth(4), .dataWidth(1)) rom_1 (.addr(CUOUT[7:4]));  // open: data
  Decoder #(.select(2), .enable("false")) decoder_1 (
    .out0(IRI_OUT), .out1(decoder_1_out1), .out2(decoder_1_out2), .out3(decoder_1_out3), .sel(CUCTR_q));
  assign {OUTFLAG, INFLAG} = cu_rom_data & bit_extender_1_out;  // AND_Gate and_1, 7 bits wide
  assign bit_extender_1_out = {{6{decoder_1_out2}}, decoder_1_out2};  // Bit_Extender bit_extender_1
  and and_2 (and_2_out, undriven, decoder_1_out1);
  and and_3 (and_3_out, undriven_2, decoder_1_out2);
  or or_1 (PCC, and_2_out, IRI_OUT, and_3_out);

  // Other names for the same wires on the sheet: INSTYPE[3:0] = CUOUT[7:4]

  // Notes on the sheet:
  //   contents of cu_rom (hex, n*v repeats v):
  //   16*0 25 26 34 26 44 45 10*0 20 20 40 20 20 0 40 40 8*0 32*70 32*34 54 55 56 13*0 64 65 66 13*0 22 32
  //   42 23 33 43 10*0 14 15 16 13*0 21 31 41 61*0 f
  //   contents of ins_rom (hex, n*v repeats v):
  //   0 0 0 1 1
  //   contents of rom_1 (hex, n*v repeats v):
  //   0 0 0 1 1 0 0 1
  //   after the first clock cycle
  //   If load or jmp instruction, we should activate PC
endmodule

module jmp (
  input  [7:0] JMPINS,
  input  OE,
  input  ZIN,
  input  OIN,
  input  CIN,
  input  SIN,
  input  [15:0] PCIN,
  input  [7:0] DATABUS,
  input  CLK,
  input  RESET,
  output PCOE,
  output [15:0] PCOUT
);

  wire bitselector_1_out;
  wire [4:0] rom_1_data;
  wire [7:0] HIGHBITS_q;
  wire [10:2] not_2_out;
  wire [15:0] adder_1_out;

  ROM #(.dataWidth(5)) rom_1 (.addr(JMPINS), .data(rom_1_data));
  Register HIGHBITS (.D(DATABUS), .clk(CLK), .Q(HIGHBITS_q), .clr(RESET));  // open: en
  or or_1 (not_2_out[4], ZIN, CIN);
  xor xor_1 (not_2_out[7], OIN, SIN);
  not not_1 (not_2_out[9], not_2_out[7]);
  not not_2 (not_2_out[2], ZIN);
  not not_3 (not_2_out[5], not_2_out[4]);
  not not_4 (not_2_out[6], CIN);
  or or_2 (not_2_out[8], ZIN, not_2_out[7]);
  and and_1 (not_2_out[10], not_2_out[9], ~ZIN);  // AND_Gate
  Adder #(.width(16)) adder_1 (.a(PCIN), .b({HIGHBITS_q, DATABUS}), .out(adder_1_out));  // open: cin, cout
  Multiplexer #(.width(16)) multiplexer_1 (
    .in0({HIGHBITS_q, DATABUS}), .in1(adder_1_out), .out(PCOUT), .sel(rom_1_data[4]), .en(PCOE));
  and and_2 (PCOE, OE, bitselector_1_out);
  BitSelector #(.width(11)) bitselector_1 (
    .in({not_2_out[10:4], CIN, not_2_out[2], ZIN, 1'b1}), .out(bitselector_1_out), .sel(rom_1_data[3:0]));

  // Notes on the sheet:
  //   contents of rom_1 (hex, n*v repeats v):
  //   49*0 1 2 3 4 5 6 7 8 9 a 6*0 11 12 13 14 15 16 17 18 19 1a
  //   =
  //   !=
  //   <
  //   <=
  //   >=
  //   < s
  //   > s
  //   >
  //   <= s
  //   >= s
endmodule

module cmp (
  input  [7:0] CMPIN,
  input  OVERFLOW,
  input  CARRY,
  input  OE,
  input  CLK,
  input  RESET,
  output ZFLAGO,
  output OFLAGO,
  output CFLAGO,
  output SFLAGO
);

  wire and_1_out, and_2_out;

  and and_1 (and_1_out, ~CMPIN[0], ~CMPIN[1], ~CMPIN[2], ~CMPIN[3], ~CMPIN[4], ~CMPIN[5], ~CMPIN[6], ~CMPIN[7]);  // AND_Gate
  D_Flip_Flop ZFLAG (.D(and_1_out), .clk(and_2_out), .Q(ZFLAGO), .reset(RESET));  // open: Qn, preset
  and and_2 (and_2_out, OE, CLK);
  D_Flip_Flop OFLAG (.D(OVERFLOW), .clk(and_2_out), .Q(OFLAGO), .reset(RESET));  // open: Qn, preset
  D_Flip_Flop CFLAG (.D(CARRY), .clk(and_2_out), .Q(CFLAGO), .reset(RESET));  // open: Qn, preset
  D_Flip_Flop SFLAG (.D(CMPIN[7]), .clk(and_2_out), .Q(SFLAGO), .reset(RESET));  // open: Qn, preset
endmodule
